// Logisim project multiplexer 3x8.circ as structural Verilog: 1 circuit, main circuit main
module main (
  input  [31:0] in_1,
  input  [31:0] in_2,
  input  [31:0] in_3,
  input  [31:0] in_4,
  input  [31:0] in_5,
  input  [2:0] in_6,
  input  [31:0] in_7,
  input  [31:0] in_8,
  input  [31:0] in_9,
  output [31:0] out_10
);

  wire a00, a01, a02, a03, a04, a05, a06, a07;

  assign out_10 = a00 ? in_1 : 32'bz;  // Controlled_Buffer controlled_buffer_1
  assign out_10 = a01 ? in_2 : 32'bz;  // Controlled_Buffer controlled_buffer_2
  assign out_10 = a02 ? in_3 : 32'bz;  // Controlled_Buffer controlled_buffer_3
  assign out_10 = a03 ? in_4 : 32'bz;  // Controlled_Buffer controlled_buffer_4
  assign out_10 = a04 ? in_5 : 32'bz;  // Controlled_Buffer controlled_buffer_5
  assign out_10 = a05 ? in_7 : 32'bz;  // Controlled_Buffer controlled_buffer_6
  assign out_10 = a06 ? in_8 : 32'bz;  // Controlled_Buffer controlled_buffer_7
  assign out_10 = a07 ? in_9 : 32'bz;  // Controlled_Buffer controlled_buffer_8
  Decoder #(.select(3)) decoder_1 (
    .out0(a00), .out1(a01), .out2(a02), .out3(a03), .out4(a04), .out5(a05), .out6(a06), .out7(a07), .sel(in_6));  // open: en

  // Other names for the same wires on the sheet: out[31:0] = out_10
endmodule
